// Logisim project cpu.circ as structural Verilog
module Instruction_Decoder (
  input  [15:0] Instruction,
  output [3:0] Opcode,
  output [2:0] RS,
  output [2:0] RT,
  output [3:0] Shamt,
  output [7:0] Immediate,
  output Shdir,
  output Unsigned,
  output SubOpp
);


  assign Immediate = Instruction[7:0];
  assign Opcode = Instruction[15:12];
  assign RS = Instruction[11:9];
  assign RT = Instruction[8:6];
  assign Shamt = Instruction[4:1];
  assign Shdir = Instruction[5];
  assign SubOpp = Instruction[0];
  assign Unsigned = Instruction[8];
endmodule

module Register_File (
  input  [7:0] Write_Data,
  input  Clock,
  input  Write_Enable,
  input  [1:0] Read_Register_1,
  input  [1:0] Write_Address,
  input  [1:0] Read_Register_2,
  output [7:0] Read_Data_1,
  output [7:0] Read_Data_2
);

  wire and_1_out, and_2_out, and_3_out, and_4_out, decoder_1_out0, decoder_1_out1, decoder_1_out2,
       decoder_1_out3;
  wire [7:0] R0_q, R1_q, R2_q, R3_q;

  Decoder #(.select(2)) decoder_1 (
    .out0(decoder_1_out0), .out1(decoder_1_out1), .out2(decoder_1_out2), .out3(decoder_1_out3),
    .sel(Write_Address));  // open: en
  and and_1 (and_1_out, Write_Enable, decoder_1_out0);
  and and_2 (and_2_out, Write_Enable, decoder_1_out1);
  and and_3 (and_3_out, Write_Enable, decoder_1_out2);
  and and_4 (and_4_out, Write_Enable, decoder_1_out3);
  Register R0 (.D(Write_Data), .en(and_1_out), .Q(R0_q), .clk(Clock));  // open: clr
  Register R1 (.D(Write_Data), .en(and_2_out), .Q(R1_q), .clk(Clock));  // open: clr
  Register R2 (.D(Write_Data), .en(and_3_out), .Q(R2_q), .clk(Clock));  // open: clr
  Register R3 (.D(Write_Data), .en(and_4_out), .Q(R3_q), .clk(Clock));  // open: clr
  Multiplexer #(.select(2), .width(8)) multiplexer_1 (
    .in0(R0_q), .in1(R1_q), .in2(R2_q), .in3(R3_q), .out(Read_Data_1), .sel(Read_Register_1));  // open: en
  Multiplexer #(.select(2), .width(8)) multiplexer_2 (
    .in0(R0_q), .in1(R1_q), .in2(R2_q), .in3(R3_q), .out(Read_Data_2), .sel(Read_Register_2));  // open: en
endmodule
